// Logisim project P2.1_Half Adder.circ as structural Verilog: 1 circuit, main circuit main
module main (
  input  A,
  input  B,
  output SUM,
  output CARRY
);

  and and_1 (CARRY, B, A);
  xor xor_1 (SUM, A, B);

  // Notes on the sheet:
  //   P 2.1 : Design Half Adder Circuit
  //   En No : 23BEIT30037
  //   (S)
  //   (C)
endmodule
