// Logisim project P2.2_Full Adder Circuit.circ as structural Verilog: 1 circuit, main circuit main
module main (
  input  A,
  input  B,
  input  Cin,
  output SUM,
  output Carry_Out
);

  wire AND_2_out, AND_out, X_OR_out;

  xor X_OR (X_OR_out, A, B);
  and AND (AND_out, Cin, X_OR_out);
  and AND_2 (AND_2_out, A, B);
  xor X_OR_2 (SUM, X_OR_out, Cin);
  or OR (Carry_Out, AND_out, AND_2_out);
endmodule
