// Logisim project P2.3 4 Bit Full Adder.circ as structural Verilog: 2 circuits, main circuit main
module main (
  input  in_1,
  input  in_2,
  input  in_3,
  input  in_4,
  input  in_5,
  input  in_6,
  input  in_7,
  input  in_8,
  input  in_9,
  output out_10,
  output out_11,
  output out_12,
  output out_13,
  output out_14
);

  wire main_2_carry_out, main_3_carry_out, main_4_carry_out, xor_1_out, xor_2_out, xor_3_out, xor_4_out;

  P2_2_Full_Adder_Circuit_main main_1 (
    .A(main_2_carry_out), .B(in_2), .Cin(xor_1_out), .SUM(out_11), .Carry_Out(out_10));
  xor xor_1 (xor_1_out, in_1, in_9);
  xor xor_2 (xor_2_out, in_3, in_9);
  P2_2_Full_Adder_Circuit_main main_2 (
    .A(main_3_carry_out), .B(in_4), .Cin(xor_2_out), .SUM(out_12), .Carry_Out(main_2_carry_out));
  P2_2_Full_Adder_Circuit_main main_3 (
    .A(main_4_carry_out), .B(in_6), .Cin(xor_3_out), .SUM(out_13), .Carry_Out(main_3_carry_out));
  xor xor_3 (xor_3_out, in_5, in_9);
  xor xor_4 (xor_4_out, in_7, in_9);
  P2_2_Full_Adder_Circuit_main main_4 (.A(in_9), .B(in_8), .Cin(xor_4_out), .SUM(out_14), .Carry_Out(main_4_carry_out));
endmodule

module _4_Bit_Adder (
  input  B3,
  input  A3,
  input  B2,
  input  A2,
  input  Bo,
  input  A0,
  input  B1,
  input  A1,
  input  Cin,
  output out_10,
  output Sum_0__S0,
  output Sum_1__S1,
  output Sum_2__S2,
  output Sum_3__S3
);

  wire main_1_carry_out, main_2_carry_out, main_3_carry_out;

  P2_2_Full_Adder_Circuit_main main_1 (.A(A0), .B(Bo), .Cin(Cin), .SUM(Sum_0__S0), .Carry_Out(main_1_carry_out));
  P2_2_Full_Adder_Circuit_main main_2 (
    .A(A1), .B(B1), .Cin(main_1_carry_out), .SUM(Sum_1__S1), .Carry_Out(main_2_carry_out));
  P2_2_Full_Adder_Circuit_main main_3 (
    .A(A2), .B(B2), .Cin(main_2_carry_out), .SUM(Sum_2__S2), .Carry_Out(main_3_carry_out));
  P2_2_Full_Adder_Circuit_main main_4 (.A(A3), .B(B3), .Cin(main_3_carry_out), .SUM(Sum_3__S3), .Carry_Out(out_10));

  // Notes on the sheet:
  //   Design 4 Bit Full Adder Circuit LogiSim
  //   Carry Out (Cout)
endmodule
