// Logisim project PR_1.2 all logic gates.circ as structural Verilog: 1 circuit, main circuit main
module main (
  input  A,
  input  in_2,
  input  A_2,
  input  B,
  input  in_5,
  input  B_2,
  input  in_7,
  input  A_3,
  input  in_9,
  input  A_4,
  input  in_11,
  input  B_3,
  input  in_13,
  output C,
  output out_15,
  output C_2,
  output C_3,
  output out_18,
  output C_4,
  output out_20
);

  and AND (C_2, A_2, B_2);
  not not_1 (C_3, A_3);
  or OR (C_4, A_4, B_3);
  nand NAND (C, A, B);
  nor NOR (out_18, in_7, in_9);
  xor XOR (out_20, in_11, in_13);
  xnor X_NOR (out_15, in_2, in_5);

  // Notes on the sheet:
  //   Practical 1.2  -  Perform Logic Gate Operation 
endmodule
