// Logisim project PR_1.3  Design a circuit for given expression  .circ as structural Verilog: 1 circuit, main circuit main
module main (
  input  in_1,
  input  in_2,
  input  in_3,
  output out_4
);

  wire NOT_out, OR_out;

  not NOT (NOT_out, in_1);
  or OR (OR_out, in_2, in_3);
  and AND (out_4, NOT_out, OR_out);

  // Notes on the sheet:
  //   PR_1.3  Design a circuit for given expression and test it, D=A'(B+C)
endmodule
