// Logisim project PR_2.1Half adder .circ as structural Verilog: 1 circuit, main circuit main
module main (
  input  A,
  input  B,
  output S,
  output C
);

  xor XOR (S, A, B);
  and AND (C, A, B);

  // Notes on the sheet:
  //   PR_2.1 Design of Half adder
endmodule
