// Logisim project PR_2.2 Full adder.circ as structural Verilog: 1 circuit, main circuit main
module main (
  input  A,
  input  B,
  input  Cin,
  output S,
  output C
);

  wire AND_2_out, AND_out, XOR_out;

  xor XOR (XOR_out, A, B);
  xor XOR_2 (S, XOR_out, Cin);
  and AND (AND_out, Cin, XOR_out);
  and AND_2 (AND_2_out, B, A);
  or OR (C, AND_out, AND_2_out);

  // Notes on the sheet:
  //   PR_2.2  Design of Full adder
endmodule
