// Logisim project PR_3 4 bit binary adder subtractor  .circ as structural Verilog: 1 circuit, main circuit main
module main (
  input  B3,
  input  A3,
  input  B2,
  input  A2,
  input  B1,
  input  A1,
  input  B0,
  input  A0,
  input  M,
  output C_OUT,
  output S3,
  output S2,
  output S1,
  output S0
);

  wire main_1_p4, main_2_p4, main_3_p4, xor_1_out, xor_2_out, xor_3_out, xor_4_out;

  xor xor_1 (xor_1_out, M, B3);
  xor xor_2 (xor_2_out, M, B2);
  // _2_2_main main_1: pin names not known; wires that end beside it: xor_1_out, A3, C_OUT, main_1_p4, S3
  xor xor_3 (xor_3_out, M, B1);
  // _2_2_main main_2: pin names not known; wires that end beside it: xor_2_out, A2, main_1_p4, main_2_p4, S2
  // _2_2_main main_3: pin names not known; wires that end beside it: xor_3_out, A1, main_2_p4, main_3_p4, S1
  xor xor_4 (xor_4_out, M, B0);
  // _2_2_main main_4: pin names not known; wires that end beside it: xor_4_out, A0, main_3_p4, M, S0

  // Notes on the sheet:
  //   P3 _To study and perform Binary Adder - Substractor (for 4-bit data)
  //   225SBECE30010
endmodule
